# Fritzing sketch TarefaExtra (saved by Fritzing 0.9.2b)
breadboards: 1

parts:
  Part1 = Arduino Uno (Rev3)
  T1 = LM35 Temperature Sensor [package="TO92 [THT]"]
  LED1 = LED - 5mm [color="Red (633nm)" package="5 mm [THT]"]
  LED2 = LED - 5mm [color="Red (633nm)" package="5 mm [THT]"]
  LED3 = LED - 5mm [color="Yellow (595nm)" package="5 mm [THT]"]
  LED4 = LED - 5mm [color="Yellow (595nm)" package="5 mm [THT]"]
  LED5 = LED - 5mm [color="Green (570nm)" package="5 mm [THT]"]
  LED6 = LED - 5mm [color="Green (570nm)" package="5 mm [THT]"]
  R1 = Resistor [tolerance=±5% resistance=220 package=THT]
  R2 = Resistor [tolerance=±5% resistance=220 package=THT]
  R3 = Resistor [tolerance=±5% resistance=220 package=THT]

nets:
  N1: Part1.A0, T1.Vout
  N2: Part1.D11_PWM/MOSI, R2.Pin_0
  N3: Part1.D12/MISO, R3.Pin_0
  N4: Part1.D13/SCK, LED1.anode, LED2.cathode, LED5.anode, LED6.cathode, R1.Pin_0, R1.Pin_1
  N5: Part1.5V, T1.+Vs
  GND: Part1.GND, T1.GND
  N6: LED1.cathode, LED2.anode, LED3.cathode, LED4.anode, R2.Pin_1
  N7: LED3.anode, LED4.cathode, LED5.cathode, LED6.anode, R3.Pin_1
